# Fritzing sketch FritzingDiagramLab5 (saved by Fritzing 0.9.9b)
breadboards: 1

parts:
  Part1 = Arduino Uno (Rev3)
  LED1 = smd LED [color="Red (633nm)" package="0805 [SMD]"]
  LED2 = smd LED [color="Red (633nm)" package="0805 [SMD]"]
  LED3 = smd LED [color="Red (633nm)" package="0805 [SMD]"]
  LED4 = smd LED [color="Red (633nm)" package="0805 [SMD]"]
  LED5 = smd LED [color="Red (633nm)" package="0805 [SMD]"]
  R1 = Resistor [tolerance=±5% resistance=220 package="2512 [SMD]"]
  R2 = Resistor [tolerance=±5% resistance=220 package="2512 [SMD]"]
  R3 = Resistor [tolerance=±5% resistance=220 package="2512 [SMD]"]
  R4 = Resistor [tolerance=±5% resistance=220 package="2512 [SMD]"]
  R5 = Resistor [tolerance=±5% resistance=220 package="2512 [SMD]"]
  R6 = Rotary Potentiometer (Small) [maximum_resistance=100kΩ package=THT]

nets:
  N1: Part1.A0, R6.wiper
  N2: Part1.D3_PWM, LED5.anode, R5.Pin_0, R5.Pin_1
  N3: Part1.D4, LED4.anode, R4.Pin_0, R4.Pin_1
  N4: Part1.D5_PWM, LED3.anode, R3.Pin_0, R3.Pin_1
  N5: Part1.D6_PWM, LED2.anode, R2.Pin_0, R2.Pin_1
  N6: Part1.D7, LED1.anode, R1.Pin_0, R1.Pin_1
  N7: Part1.5V, R6.leg1
  N8: Part1.GND, LED1.cathode, LED2.cathode, LED3.cathode, LED4.cathode, LED5.cathode, R6.leg2
